// Digital circuit 8Bit-DIY-CPU.dig as structural Verilog
module _8Bit_DIY_CPU (
  input  clk,
  input  in_2
);

  wire A_0, A_1, A_2, A_E, A_O, and_1_out, and_2_out, and_3_out, button_1_out, button_2_out, C, C_E, C_F,
       C_J, C_O, E_E, E_F, M, M_O, MA_I, MR_I, MR_O, not_1_out, or_1_out, R_W, S_0, S_1, S_2, S_3;
  wire [7:0] ramsingleportsel_1_d, register_1_q, register_2_q;

  Button button_1 (.out(button_1_out));
  and and_1 (and_1_out, clk, in_2);
  Button button_2 (.out(button_2_out));
  or or_1 (or_1_out, and_1_out, button_1_out);
  // Probe on ramsingleportsel_1_d
  Register #(.Bits(8)) register_1 (.D(ramsingleportsel_1_d), .C(or_1_out), .en(MA_I), .Q(register_1_q));
  RAMSinglePortSel #(.AddrBits(8), .Bits(8)) ramsingleportsel_1 (
    .A(register_1_q), .CS(1'b1), .WE(R_W), .OE(M_O), .D(ramsingleportsel_1_d));
  _8Bit_DIY_CPU_ALU _8bit_diy_cpu_alu_1 (
    .BUS_I(ramsingleportsel_1_d), .A_E(A_E), .A_O(A_O), .S_0(S_0), .S_1(S_1), .S_2(S_2), .S_3(S_3), .C(C),
    .M(M), .CLK(or_1_out), .RST(button_2_out), .BUS_O(ramsingleportsel_1_d), .C_F(C_F), .E_F(E_F));
  _8Bit_DIY_CPU_MR _8bit_diy_cpu_mr_1 (
    .BUS_I(ramsingleportsel_1_d), .MR_I(MR_I), .MR_O(MR_O), .CLK(or_1_out), .RST(button_2_out),
    .BUS_O(ramsingleportsel_1_d));
  _8Bit_DIY_CPU_PC _8bit_diy_cpu_pc_1 (
    .BUS_O(ramsingleportsel_1_d), .BUS_I(ramsingleportsel_1_d), .C_O(C_O), .C_E(C_E), .C_J(C_J),
    .CLK(or_1_out), .RST(button_2_out));
  _8Bit_DIY_CPU_CONTROLL _8bit_diy_cpu_controll_1 (
    .BUS_I(ramsingleportsel_1_d), .E_F(E_F), .C_F(C_F), .CLK(not_1_out), .RST(button_2_out), .C_J(C_J),
    .C_E(C_E), .C_O(C_O), .MR_I(MR_I), .MR_O(MR_O), .R_W(R_W), .MA_I(MA_I), .M_O(M_O), .S_0(S_0), .S_1(S_1),
    .S_2(S_2), .S_3(S_3), .C(C), .M(M), .A_E(A_E), .A_O(A_O), .A_2(A_2), .A_1(A_1), .A_0(A_0), .E_E(E_E));
  not not_1 (not_1_out, or_1_out);
  and and_2 (and_2_out, E_E, ~R_W);  // And
  and and_3 (and_3_out, E_E, R_W);
  Register #(.Bits(8)) register_2 (.D(ramsingleportsel_1_d), .C(or_1_out), .en(and_2_out), .Q(register_2_q));
  ROM #(.AddrBits(8), .Bits(8)) rom_1 (.A(register_2_q), .sel(and_3_out), .D(ramsingleportsel_1_d));

  // Notes on the sheet:
  //   clk: Hz: 50
  //   RST
  //   CLK
  //   Data BUS
  //   contents of rom_1 (hex, n*v repeats v):
  //   1,5,13,3,d0,8,f0,8*0,ff,15*0,ff,15*0,ff,15*0,ff,15*0,ff,15*0,ff
  //   ,15*0,ff,15*0,ff,15*0,ff,15*0,ff,15*0,ff,15*0,ff,15*0,ff,15*0
  //   ,ff,15*0,ff,15*0,ff
endmodule
