// Digital circuit 8Bit-DIY-CPU_ALU.dig as structural Verilog
module _8Bit_DIY_CPU_ALU (
  input  [7:0] BUS_I,
  input  CLK,
  input  A_E,
  input  S_0,
  input  S_1,
  input  S_2,
  input  S_3,
  input  C,
  input  RST,
  input  A_O,
  input  M,
  output [7:0] BUS_O,
  output C_F,
  output E_F
);

  wire _74173_1_pin9, _74173_1_pin11, _74173_1_pin12, _74173_1_pin13, _74173_1_pin14, _74173_2_pin11,
       _74173_2_pin12, _74173_2_pin13, _74173_2_pin14, _74173_5_pin11, _74173_5_pin12, _74173_5_pin14,
       _74181_2_pin7, _74541_1_pin1, and_1_out, B0, B1, B2, B3, B4, B5, B6, B7, F0, F1, F2, F3, F4, F5, F6,
       F7, not_1_out, undriven, undriven_2, undriven_3;

  _74181 _74181_1 (
    .pin1(B0), .pin2(BUS_I[0]), .pin3(S_3), .pin4(S_2), .pin5(S_1), .pin6(S_0), .pin7(C), .pin8(M),
    .pin9(F0), .pin10(F1), .pin11(F2), .pin12(1'b0));  // open: pin13, pin14, pin15, pin16, pin17, pin18, pin19, pin20, pin21, pin22, pin23, pin24
  not not_1 (not_1_out, CLK);
  _74173 _74173_1 (
    .pin1(1'b0), .pin2(1'b0), .pin3(B0), .pin4(B1), .pin5(B2), .pin6(B3), .pin7(not_1_out), .pin8(1'b0),
    .pin9(_74173_1_pin9), .pin10(_74173_1_pin9), .pin11(_74173_1_pin11), .pin12(_74173_1_pin12),
    .pin13(_74173_1_pin13), .pin14(_74173_1_pin14), .pin15(RST), .pin16(1'b1));
  _74173 _74173_2 (
    .pin1(1'b0), .pin2(1'b0), .pin3(B4), .pin4(B5), .pin5(B6), .pin6(B7), .pin7(not_1_out), .pin8(1'b0),
    .pin9(_74173_1_pin9), .pin10(_74173_1_pin9), .pin11(_74173_2_pin11), .pin12(_74173_2_pin12),
    .pin13(_74173_2_pin13), .pin14(_74173_2_pin14), .pin15(RST), .pin16(1'b1));
  not not_2 (_74173_1_pin9, A_E);
  _74173 _74173_3 (
    .pin1(1'b0), .pin2(1'b0), .pin3(_74173_1_pin14), .pin4(_74173_1_pin13), .pin5(_74173_1_pin12),
    .pin6(_74173_1_pin11), .pin7(CLK), .pin8(1'b0), .pin9(_74173_1_pin9), .pin10(_74173_1_pin9), .pin11(F3),
    .pin12(F2), .pin13(F1), .pin14(F0), .pin15(RST), .pin16(1'b1));
  _74173 _74173_4 (
    .pin1(1'b0), .pin2(1'b0), .pin3(_74173_2_pin14), .pin4(_74173_2_pin13), .pin5(_74173_2_pin12),
    .pin6(_74173_2_pin11), .pin7(CLK), .pin8(1'b0), .pin9(_74173_1_pin9), .pin10(_74173_1_pin9), .pin11(F7),
    .pin12(F6), .pin13(F5), .pin14(F4), .pin15(RST), .pin16(1'b1));
  _74181 _74181_2 (
    .pin1(B4), .pin2(BUS_I[4]), .pin3(S_3), .pin4(S_2), .pin5(S_1), .pin6(S_0), .pin7(_74181_2_pin7),
    .pin8(M), .pin9(F4), .pin10(F5), .pin11(F6), .pin12(1'b0));  // open: pin13, pin14, pin15, pin16, pin17, pin18, pin19, pin20, pin21, pin22, pin23, pin24
  and and_1 (and_1_out, undriven_2, undriven);
  _74173 _74173_5 (
    .pin1(1'b0), .pin2(1'b0), .pin3(C_F), .pin4(E_F), .pin7(CLK), .pin8(1'b0), .pin9(_74173_1_pin9),
    .pin10(_74173_1_pin9), .pin11(_74173_5_pin11), .pin12(_74173_5_pin12), .pin13(and_1_out),
    .pin14(_74173_5_pin14), .pin15(RST), .pin16(1'b1));  // open: pin5, pin6
  // NotConnected on _74173_5_pin12
  // NotConnected on _74173_5_pin11
  not not_3 (_74173_5_pin14, undriven_3);
  _74541 _74541_1 (
    .pin1(_74541_1_pin1), .pin2(B0), .pin3(B1), .pin4(B2), .pin5(B3), .pin6(B4), .pin7(B5), .pin8(B6),
    .pin9(B7), .pin10(1'b0), .pin11(BUS_O[7]), .pin12(BUS_O[6]), .pin13(BUS_O[5]), .pin14(BUS_O[4]),
    .pin15(BUS_O[3]), .pin16(BUS_O[2]), .pin17(BUS_O[1]), .pin18(BUS_O[0]), .pin19(_74541_1_pin1),
    .pin20(1'b1));
  not not_4 (_74541_1_pin1, A_O);

  // Other names for the same wires on the sheet: A0 = BUS_I[0]; A1 = BUS_I[1]; A2 = BUS_I[2]; A3 = BUS_I[3];
  //   A4 = BUS_I[4]; A5 = BUS_I[5]; A6 = BUS_I[6]; A7 = BUS_I[7]; O0 = BUS_O[0]; O1 = BUS_O[1]; O2 = BUS_O[2];
  //   O3 = BUS_O[3]; O4 = BUS_O[4]; O5 = BUS_O[5]; O6 = BUS_O[6]; O7 = BUS_O[7]; S0 = S_0; S1 = S_1; S2 = S_2;
  //   S3 = S_3
endmodule
