// Digital circuit 8Bit-DIY-CPU_CONTROLL.dig as structural Verilog
module _8Bit_DIY_CPU_CONTROLL (
  input  [7:0] BUS_I,
  input  E_F,
  input  C_F,
  input  CLK,
  input  RST,
  output S_0,
  output S_1,
  output S_2,
  output S_3,
  output C,
  output C_J,
  output C_E,
  output C_O,
  output R_W,
  output MA_I,
  output M_O,
  output A_E,
  output E_E,
  output A_O,
  output A_2,
  output A_0,
  output A_1,
  output MR_I,
  output MR_O,
  output M
);

  wire _7474_1_pin9, _7474_1_pin10, _7474_1_pin13, _74161_1_pin3, _74161_1_pin4, _74161_1_pin5,
       _74161_1_pin6, _74173_1_pin9, and_1_out, and_2_out, and_3_out, B_F, C0, C1, C2, C_JC, C_JE, C_JJ, I_0,
       I_1, I_2, I_3, I_4, I_5, I_6, I_7, IR_I, not_1_out, not_3_out, not_4_out, or_1_out, RST_BF, RST_SC;

  and and_1 (and_1_out, RST_SC, CLK);
  or or_1 (or_1_out, and_1_out, RST);
  not not_1 (not_1_out, or_1_out);
  _74161 _74161_1 (
    .pin1(not_1_out), .pin2(CLK), .pin3(_74161_1_pin3), .pin4(_74161_1_pin4), .pin5(_74161_1_pin5),
    .pin6(_74161_1_pin6), .pin7(1'b1), .pin8(1'b0), .pin9(1'b1), .pin10(1'b1), .pin12(C2), .pin13(C1),
    .pin14(C0), .pin16(1'b1));  // open: pin11, pin15
  // NotConnected on _74161_1_pin3
  // NotConnected on _74161_1_pin4
  // NotConnected on _74161_1_pin5
  // NotConnected on _74161_1_pin6
  _74173 _74173_1 (
    .pin1(1'b0), .pin2(1'b0), .pin3(I_0), .pin4(I_1), .pin5(I_2), .pin6(I_3), .pin7(CLK), .pin8(1'b0),
    .pin9(_74173_1_pin9), .pin10(_74173_1_pin9), .pin11(BUS_I[3]), .pin12(BUS_I[2]), .pin13(BUS_I[1]),
    .pin14(BUS_I[0]), .pin15(RST), .pin16(1'b1));
  _74173 _74173_2 (
    .pin1(1'b0), .pin2(1'b0), .pin3(I_4), .pin4(I_5), .pin5(I_6), .pin6(I_7), .pin7(CLK), .pin8(1'b0),
    .pin9(_74173_1_pin9), .pin10(_74173_1_pin9), .pin11(BUS_I[7]), .pin12(BUS_I[6]), .pin13(BUS_I[5]),
    .pin14(BUS_I[4]), .pin15(RST), .pin16(1'b1));
  not not_2 (_74173_1_pin9, IR_I);
  not not_3 (not_3_out, CLK);
  not not_4 (not_4_out, RST);
  _7474 _7474_1 (
    .pin1(1'b1), .pin2(RST_BF), .pin3(not_3_out), .pin4(not_4_out), .pin5(B_F), .pin7(1'b0), .pin8(RST_BF),
    .pin9(_7474_1_pin9), .pin10(_7474_1_pin10), .pin11(CLK), .pin12(_7474_1_pin9), .pin13(_7474_1_pin13),
    .pin14(1'b1));  // open: pin6
  AT28C64_CONTROLL_programmed_part1 at28c64_controll_programmed_part1_1 ();
  not not_5 (_7474_1_pin13, RST);
  not not_6 (_7474_1_pin10, C_F);
  AT28C64_CONTROLL_programmed_part2 at28c64_controll_programmed_part2_1 ();
  and and_2 (and_2_out, C_JE, E_F);
  and and_3 (and_3_out, C_JC, C_F);
  or or_2 (C_J, and_2_out, and_3_out, C_JJ);
  and and_4 (S_0, A_E, I_4);
  and and_5 (S_1, A_E, I_3);
  and and_6 (S_2, A_E, I_2);
  and and_7 (S_3, A_E, I_1);
  and and_8 (C, A_E, I_0);
  and and_9 (M, A_E, I_5);
  and and_10 (A_2, E_E, I_5);
  and and_11 (A_1, E_E, I_6);
  and and_12 (A_0, E_E, I_7);

  // Other names for the same wires on the sheet: D0 = BUS_I[0]; D1 = BUS_I[1]; D2 = BUS_I[2]; D3 = BUS_I[3];
  //   D4 = BUS_I[4]; D5 = BUS_I[5]; D6 = BUS_I[6]; D7 = BUS_I[7]
endmodule
