// Digital circuit 8Bit-DIY-CPU_DISPLAY-prototype.dig as structural Verilog
module _8Bit_DIY_CPU_DISPLAY_prototype (
  input  [7:0] in_1,
  input  clk,
  input  [7:0] in_3
);

  wire [3:0] counter_1_out, multiplexer_1_out;
  wire [7:0] ramasync_1_q;

  Multiplexer #(.Bits(4)) multiplexer_1 (
    .sel(in_3[6]), .in_0(in_3[3:0]), .in_1(counter_1_out), .out(multiplexer_1_out));
  RAMAsync #(.AddrBits(4), .Bits(8)) ramasync_1 (.A(multiplexer_1_out), .D(in_1), .we(in_3[7]), .Q(ramasync_1_q));
  Counter #(.Bits(4)) counter_1 (.en(1'b1), .C(clk), .clr(1'b0), .out(counter_1_out));  // open: ovf
  LedMatrix #(.colAddrBits(4), .ledPersistence("true")) ledmatrix_1 (.rows(ramasync_1_q), .column(counter_1_out));

  // Notes on the sheet:
  //   clk: Hz: 50
endmodule
