// Digital circuit 8Bit-DIY-CPU_MR.dig as structural Verilog
module _8Bit_DIY_CPU_MR (
  input  MR_I,
  input  MR_O,
  input  RST,
  input  CLK,
  input  [7:0] BUS_I,
  output [7:0] BUS_O
);

  wire _74173_1_pin9, not_2_out, O0, O1, O2, O3, O4, O5, O6, O7;

  _74173 _74173_1 (
    .pin1(1'b0), .pin2(1'b0), .pin3(O0), .pin4(O1), .pin5(O2), .pin6(O3), .pin7(CLK), .pin8(1'b0),
    .pin9(_74173_1_pin9), .pin10(_74173_1_pin9), .pin11(BUS_I[3]), .pin12(BUS_I[2]), .pin13(BUS_I[1]),
    .pin14(BUS_I[0]), .pin15(RST), .pin16(1'b1));
  _74173 _74173_2 (
    .pin1(1'b0), .pin2(1'b0), .pin3(O4), .pin4(O5), .pin5(O6), .pin6(O7), .pin7(CLK), .pin8(1'b0),
    .pin9(_74173_1_pin9), .pin10(_74173_1_pin9), .pin11(BUS_I[7]), .pin12(BUS_I[6]), .pin13(BUS_I[5]),
    .pin14(BUS_I[4]), .pin15(RST), .pin16(1'b1));
  not not_1 (_74173_1_pin9, MR_I);
  not not_2 (not_2_out, MR_O);
  _74541 _74541_1 (
    .pin1(not_2_out), .pin2(O0), .pin3(O1), .pin4(O2), .pin5(O3), .pin6(O4), .pin7(O5), .pin8(O6), .pin9(O7),
    .pin10(1'b0), .pin11(BUS_O[7]), .pin12(BUS_O[6]), .pin13(BUS_O[5]), .pin14(BUS_O[4]), .pin15(BUS_O[3]),
    .pin16(BUS_O[2]), .pin17(BUS_O[1]), .pin18(BUS_O[0]), .pin19(not_2_out), .pin20(1'b1));

  // Other names for the same wires on the sheet: D0 = BUS_I[0]; D1 = BUS_I[1]; D2 = BUS_I[2]; D3 = BUS_I[3];
  //   D4 = BUS_I[4]; D5 = BUS_I[5]; D6 = BUS_I[6]; D7 = BUS_I[7]; Q0 = BUS_O[0]; Q1 = BUS_O[1]; Q2 = BUS_O[2];
  //   Q3 = BUS_O[3]; Q4 = BUS_O[4]; Q5 = BUS_O[5]; Q6 = BUS_O[6]; Q7 = BUS_O[7]
endmodule
