// Digital circuit 8Bit-DIY-CPU_PC.dig as structural Verilog
module _8Bit_DIY_CPU_PC (
  input  [7:0] BUS_I,
  input  RST,
  input  C_E,
  input  CLK,
  input  C_J,
  input  C_O,
  output [7:0] BUS_O
);

  wire _74161_1_pin9, _74161_1_pin15, C0, C1, C2, C3, C4, C5, C6, C7, not_1_out, not_2_out;

  not not_1 (not_1_out, RST);
  _74161 _74161_1 (
    .pin1(not_1_out), .pin2(CLK), .pin3(BUS_I[0]), .pin4(BUS_I[1]), .pin5(BUS_I[2]), .pin6(BUS_I[3]),
    .pin7(C_E), .pin8(1'b0), .pin9(_74161_1_pin9), .pin10(C_E), .pin11(C3), .pin12(C2), .pin13(C1),
    .pin14(C0), .pin15(_74161_1_pin15), .pin16(1'b1));
  _74161 _74161_2 (
    .pin1(not_1_out), .pin2(CLK), .pin3(BUS_I[4]), .pin4(BUS_I[5]), .pin5(BUS_I[6]), .pin6(BUS_I[7]),
    .pin7(C_E), .pin8(1'b0), .pin9(_74161_1_pin9), .pin10(_74161_1_pin15), .pin11(C7), .pin12(C6),
    .pin13(C5), .pin14(C4), .pin16(1'b1));  // open: pin15
  not not_2 (not_2_out, C_O);
  not not_3 (_74161_1_pin9, C_J);
  _74541 _74541_1 (
    .pin1(not_2_out), .pin2(C0), .pin3(C1), .pin4(C2), .pin5(C3), .pin6(C4), .pin7(C5), .pin8(C6), .pin9(C7),
    .pin10(1'b0), .pin11(BUS_O[7]), .pin12(BUS_O[6]), .pin13(BUS_O[5]), .pin14(BUS_O[4]), .pin15(BUS_O[3]),
    .pin16(BUS_O[2]), .pin17(BUS_O[1]), .pin18(BUS_O[0]), .pin19(not_2_out), .pin20(1'b1));

  // Other names for the same wires on the sheet: D0 = BUS_I[0]; D1 = BUS_I[1]; D2 = BUS_I[2]; D3 = BUS_I[3];
  //   D4 = BUS_I[4]; D5 = BUS_I[5]; D6 = BUS_I[6]; D7 = BUS_I[7]; Q0 = BUS_O[0]; Q1 = BUS_O[1]; Q2 = BUS_O[2];
  //   Q3 = BUS_O[3]; Q4 = BUS_O[4]; Q5 = BUS_O[5]; Q6 = BUS_O[6]; Q7 = BUS_O[7]
endmodule
