// Digital circuit 8Bit-DIY-CPU_RAM.dig as structural Verilog
module _8Bit_DIY_CPU_RAM (
  input  [7:0] BUS_I,
  input  R_W,
  input  MA_I,
  input  CLK,
  input  RST,
  input  M_O
);

  wire _74173_1_pin9, A_0, A_1, A_2, A_3, A_4, A_5, A_6, A_7, not_2_out, not_3_out;

  _74173 _74173_1 (
    .pin1(1'b0), .pin2(1'b0), .pin3(A_0), .pin4(A_1), .pin5(A_2), .pin6(A_3), .pin7(CLK), .pin8(1'b0),
    .pin9(_74173_1_pin9), .pin10(_74173_1_pin9), .pin11(BUS_I[3]), .pin12(BUS_I[2]), .pin13(BUS_I[1]),
    .pin14(BUS_I[0]), .pin15(RST), .pin16(1'b1));
  _74173 _74173_2 (
    .pin1(1'b0), .pin2(1'b0), .pin3(A_4), .pin4(A_5), .pin5(A_6), .pin6(A_7), .pin7(CLK), .pin8(1'b0),
    .pin9(_74173_1_pin9), .pin10(_74173_1_pin9), .pin11(BUS_I[7]), .pin12(BUS_I[6]), .pin13(BUS_I[5]),
    .pin14(BUS_I[4]), .pin15(RST), .pin16(1'b1));
  not not_1 (_74173_1_pin9, MA_I);
  CY62256N cy62256n_1 (
    .A_5(A_5), .A_7(A_6), .A_9(A_7), .A_11(1'b0), .A_13(1'b0), .I_O_0(1'b0), .I_O_2(1'b0), .I_O_3(1'b0),
    .I_O_5(1'b0), .I_O_7(1'b0), .A_0(BUS_I[0]), .A_1(BUS_I[1]), .A_3(BUS_I[2]), .WE(1'b0));  // open: A_6, A_8, A_10, A_12, A_14, I_O_1, GND, I_O_4, I_O_6, CE, OE, A_2, A_4, VCC
  not not_2 (not_2_out, R_W);
  not not_3 (not_3_out, M_O);

  // Other names for the same wires on the sheet: D0 = BUS_I[0]; D1 = BUS_I[1]; D2 = BUS_I[2]; D3 = BUS_I[3];
  //   D4 = BUS_I[4]; D5 = BUS_I[5]; D6 = BUS_I[6]; D7 = BUS_I[7]; M_E = MA_I
endmodule
