// Digital circuit AT28C64.dig as structural Verilog
module AT28C64 (
  input  RDY,
  input  A12,
  input  A7,
  input  A6,
  input  A5,
  input  A4,
  input  A3,
  input  A2,
  input  A1,
  input  A0,
  input  I_O0,
  input  I_O1,
  input  I_O2,
  input  GND,
  input  I_O3,
  input  I_O4,
  input  I_O5,
  input  I_O6,
  input  I_O7,
  input  CE,
  input  A10,
  input  OE,
  input  A9,
  input  A8,
  input  NC,
  input  WE,
  input  VCC,
  input  A11
);

  wire not_1_out;
  wire [7:0] eeprom_1_d;

  EEPROM #(.AddrBits(13), .isProgramMemory("true"), .Bits(8)) eeprom_1 (
    .A({A12, A11, A10, A9, A8, A7, A6, A5, A4, A3, A2, A1, A0}), .CS(~CE), .WE(~WE), .OE(~OE), .D(eeprom_1_d));
  not not_1 (not_1_out, OE);
  BusSplitter #(.Bits(8)) bussplitter_1 (
    .D(eeprom_1_d), .OE(not_1_out), .D0(I_O0), .D1(I_O1), .D2(I_O2), .D3(I_O3), .D4(I_O4), .D5(I_O5),
    .D6(I_O6), .D7(I_O7));

  // Notes on the sheet:
  //   contents of eeprom_1 (hex, n*v repeats v):
  //   1,2,3,4,52*0,a6,4278*0,aa,15*0,ff,3839*0,ff
endmodule
