// Digital circuit AT28C64_CONTROLL-programmed-part1.dig as structural Verilog
module AT28C64_CONTROLL_programmed_part1 (
  input  RDY,
  input  A12,
  input  A7,
  input  A6,
  input  A5,
  input  A4,
  input  A3,
  input  A2,
  input  A1,
  input  A0,
  input  I_O0,
  input  I_O1,
  input  I_O2,
  input  GND,
  input  I_O3,
  input  I_O4,
  input  I_O5,
  input  I_O6,
  input  I_O7,
  input  CE,
  input  A10,
  input  OE,
  input  A9,
  input  A8,
  input  NC,
  input  WE,
  input  VCC,
  input  A11
);

  wire not_1_out, not_2_out;
  wire [7:0] rom_1_d;

  not not_1 (not_1_out, CE);
  not not_2 (not_2_out, OE);
  ROM #(.bigEndian("true"), .AddrBits(13), .Bits(8)) rom_1 (
    .A({A12, A11, A10, A9, A8, A7, A6, A5, A4, A3, A2, A1, A0}), .sel(not_1_out), .D(rom_1_d));
  assign WE = not_2_out ? 1'b1 : 1'bz;  // Driver driver_1
  BusSplitter #(.Bits(8)) bussplitter_1 (
    .D(rom_1_d), .OE(not_2_out), .D0(I_O0), .D1(I_O1), .D2(I_O2), .D3(I_O3), .D4(I_O4), .D5(I_O5), .D6(I_O6),
    .D7(I_O7));

  // Notes on the sheet:
  //   WE: default 1
  //   rom_1 loads microcode_DIY-8Bit-CPU-part1.bin
endmodule
