// Digital circuit CY62256N.dig as structural Verilog
module CY62256N (
  input  A_5,
  input  A_6,
  input  A_7,
  input  A_8,
  input  A_9,
  input  A_10,
  input  A_11,
  input  A_12,
  input  A_13,
  input  A_14,
  input  I_O_0,
  input  I_O_1,
  input  I_O_2,
  input  GND,
  input  I_O_3,
  input  I_O_4,
  input  I_O_5,
  input  I_O_6,
  input  I_O_7,
  input  CE,
  input  A_0,
  input  OE,
  input  A_1,
  input  A_2,
  input  A_3,
  input  A_4,
  input  WE,
  input  VCC
);

  wire not_1_out;
  wire [7:0] ramsingleportsel_1_d;

  RAMSinglePortSel #(.AddrBits(15), .isProgramMemory("true"), .Bits(8)) ramsingleportsel_1 (
    .A({A_14, A_13, A_12, A_11, A_10, A_9, A_8, A_7, A_6, A_5, A_4, A_3, A_2, A_1, A_0}), .CS(~CE), .WE(~WE),
    .OE(~OE), .D(ramsingleportsel_1_d));
  not not_1 (not_1_out, OE);
  BusSplitter #(.Bits(8)) bussplitter_1 (
    .D(ramsingleportsel_1_d), .OE(not_1_out), .D0(I_O_0), .D1(I_O_1), .D2(I_O_2), .D3(I_O_3), .D4(I_O_4),
    .D5(I_O_5), .D6(I_O_6), .D7(I_O_7));
endmodule
